# Fritzing sketch bomb_scheme (saved by Fritzing 0.9.2b)
breadboards: 1

parts:
  LCD1 = LCD screen
  Composant1 = Arduino Uno (Rev3)
  LED1 = LED - 5mm [color="Red (633nm)" package="5 mm [THT]"]
  R1 = Rotary Potentiometer (Small) [maximum_resistance=100kΩ package=THT]
  LED2 = LED - 5mm [color="Green (570nm)" package="5 mm [THT]"]
  S1 = Pushbutton [package=THT]
  S2 = Pushbutton [package=THT]
  S3 = Pushbutton [package=THT]
  J1 = Piezo Speaker
  KEYPAD1 = Membrane Matrix Keypad

nets:
  VSS: LCD1.VSS, LCD1.R/W, LCD1.LED-, Composant1.GND, LED1.anode, R1.leg2, LED2.anode, J1.pin1
  VDD: LCD1.VDD, LCD1.LED+, Composant1.5V, R1.leg1, S1.leg0, S2.leg0, S3.leg0
  N1: LCD1.V0, R1.wiper
  N2: LCD1.RS, Composant1.D7
  N3: LCD1.E, Composant1.D8
  N4: LCD1.DB4, Composant1.D10_PWM/SS
  N5: LCD1.DB5, Composant1.D11_PWM/MOSI
  N6: LCD1.DB6, Composant1.D12/MISO
  N7: LCD1.DB7, Composant1.D13/SCK
  N8: Composant1.A0, KEYPAD1.7
  N9: Composant1.A1, KEYPAD1.6
  N10: Composant1.A2, KEYPAD1.5
  N11: Composant1.A3, KEYPAD1.4
  N12: Composant1.A4/SDA, KEYPAD1.3
  N13: Composant1.A5/SCL, KEYPAD1.2
  N14: Composant1.D9_PWM, J1.pin2
  N15: Composant1.D1/TX, KEYPAD1.1
  N16: Composant1.D2, LED2.cathode
  N17: Composant1.D3_PWM, LED1.cathode
  N18: Composant1.D4, S3.leg1
  N19: Composant1.D5_PWM, S1.leg1
  N20: Composant1.D6_PWM, S2.leg1

custom parts:
  Membrane Matrix Keypad: Membrane Matrix 3x4 Keypad
